# Fritzing sketch Sketch (saved by Fritzing 0.9.3b)
breadboards: 1

parts:
  Arduino = Arduino Uno (Rev3)
  推杆电机 = DC Motor
  L293D = L293D [package=THT]
  CHQ1838 = TSOP312.., 314.. [package=THT]

nets:
  N1: Arduino.D9_PWM, CHQ1838.GND
  N2: Arduino.D10_PWM/SS, L293D.In_2
  N3: Arduino.D11_PWM/MOSI, L293D.In_1
  N4: Arduino.5V, L293D.Enable_1, L293D.+Vmotor, L293D.+V, CHQ1838.Data
  N5: Arduino.GND, L293D.0V, CHQ1838.Vs
  N6: 推杆电机.pin_1, L293D.Out_1_(_Controlled_by_Enable_1_)
  N7: 推杆电机.pin_2, L293D.Out_2_(_Controlled_by_Enable_1_)
